// Logisim project s-mips.circ as structural Verilog: 14 circuits, main circuit S-MIPS Board
module S_MIPS_Board (
  input  DESHABILITAR_DISPATCHER,
  output halt
);

  wire button_1_out, CLK, CS, d_ff_1_q, LCLR, LoadRAM, LoadRAMOn, LW, R_R_W, R_W, ram_dispatcher_1_finished,
       RCS, Reset_out, RST, TTY_EN;
  wire [2:0] KDB;
  wire [3:0] LMask, Mask, ram_1_read_time, ram_1_write_time, RMask;
  wire [6:0] KDB_DATA, TTY_DATA;
  wire [15:0] Addr, LAddr, RAddr;
  wire [31:0] I0, I1, I2, I3, LData, ram_1_data_out_0, ram_1_data_out_1, ram_1_data_out_2, ram_1_data_out_3,
       RI0, RI1, RI2, RI3;

  TTY #(.rows(25), .cols(80)) tty_1 (.data(TTY_DATA), .clk(CLK), .we(TTY_EN), .clr(RST));
  not not_1 (LoadRAMOn, ram_dispatcher_1_finished);
  RAM_Dispatcher ram_dispatcher_1 (
    .WriteTime(ram_1_write_time), .Clock(CLK), .Data(LData), .Address(LAddr), .Mask(LMask),
    .Finished(ram_dispatcher_1_finished), .Write(LW), .CLR(LCLR));
  Keyboard #(.buflen(64)) keyboard_1 (.clk(CLK), .re(KDB[0]), .avail(KDB[2]), .data(KDB_DATA));  // open: clr
  RAM ram_1 (
    .Address(RAddr), .Data_Out_0(ram_1_data_out_0), .Data_Out_1(ram_1_data_out_1),
    .Data_Out_2(ram_1_data_out_2), .Data_Out_3(ram_1_data_out_3), .Data_In_0(RI0), .Data_In_1(RI1),
    .Data_In_2(RI2), .Data_In_3(RI3), .Mask(RMask), .nRead_Write(R_R_W), .Chip_Select(RCS),
    .Read_Time(ram_1_read_time), .Reset(button_1_out), .Write_Time(ram_1_write_time));
  Button button_1 (.out(button_1_out));
  D_Flip_Flop d_ff_1 (.clk(CLK), .D(1'b1), .Q(d_ff_1_q), .reset(Reset_out));  // open: Qn, preset, en
  Button Reset (.out(Reset_out));
  S_MIPS s_mips_1 (
    .Kbd_Enable(KDB[0]), .Address(Addr), .Kbd_Clear(KDB[1]), .Kbd_Available(KDB[2]), .RAM_In_0(I0),
    .Kbd_ASCII_Data(KDB_DATA), .RAM_In_1(I1), .TTY_Enable(TTY_EN), .RAM_In_2(I2), .RAM_In_3(I2),
    .TTY_ASCII_Data(TTY_DATA), .Reset(RST), .RAM_Out_0(ram_1_data_out_0), .Clock(CLK),
    .RAM_Out_1(ram_1_data_out_1), .Stop(halt), .RAM_Out_2(ram_1_data_out_2), .RAM_Out_3(ram_1_data_out_3),
    .Mask(Mask), .Read_Time(ram_1_read_time), .Write_Time(ram_1_write_time), .nRead_Write(R_W),
    .Chip_Select(CS));
  D_Flip_Flop d_ff_2 (.clk(CLK), .D(d_ff_1_q), .Qn(LCLR), .reset(Reset_out));  // open: Q, preset, en
  or or_1 (RST, LCLR, LoadRAM);
  Clock clock_1 (.out(CLK));
  Multiplexer #(.width(32), .enable("false")) multiplexer_1 (.in0(I0), .in1(LData), .out(RI0), .sel(LoadRAM));
  Multiplexer #(.width(32), .enable("false")) multiplexer_2 (.in0(I1), .in1(LData), .out(RI1), .sel(LoadRAM));
  Multiplexer #(.width(32), .enable("false")) multiplexer_3 (.in0(I2), .in1(LData), .out(RI2), .sel(LoadRAM));
  Multiplexer #(.width(32), .enable("false")) multiplexer_4 (.in0(I3), .in1(LData), .out(RI3), .sel(LoadRAM));
  and and_1 (LoadRAM, ~DESHABILITAR_DISPATCHER, LoadRAMOn);  // AND_Gate
  Multiplexer #(.width(16), .enable("false")) multiplexer_5 (.in0(Addr), .in1(LAddr), .out(RAddr), .sel(LoadRAM));
  Multiplexer #(.width(4), .enable("false")) multiplexer_6 (.in0(Mask), .in1(LMask), .out(RMask), .sel(LoadRAM));
  Multiplexer #(.enable("false")) multiplexer_7 (.in0(CS), .in1(LW), .out(RCS), .sel(LoadRAM));
  Multiplexer #(.enable("false")) multiplexer_8 (.in0(R_W), .in1(LW), .out(R_R_W), .sel(LoadRAM));

  // Notes on the sheet:
  //   NO MODIFICAR
  //   Keyboard
endmodule

module RAM (
  input  [15:0] Address,
  input  [31:0] Data_In_0,
  input  [31:0] Data_In_1,
  input  [31:0] Data_In_2,
  input  [31:0] Data_In_3,
  input  [3:0] Mask,
  input  nRead_Write,
  input  Chip_Select,
  input  Reset,
  output [31:0] Data_Out_0,
  output [31:0] Data_Out_1,
  output [31:0] Data_Out_2,
  output [31:0] Data_Out_3,
  output [3:0] Read_Time,
  output [3:0] Write_Time
);

  wire and_2_out, and_3_out, and_4_out, and_5_out, and_6_out, and_7_out, and_8_out, and_9_out, Changed, CLK,
       comparator_2_eq, comparator_3_eq, comparator_4_eq, comparator_5_eq, comparator_6_eq, Count,
       demultiplexer_3_out0, Idle, Idle_q, Load, Load0, Load1, nand_1_out, or_1_out, or_2_out, or_3_out,
       or_4_out, or_5_out, or_6_out, or_7_out, or_8_out, or_9_out, or_10_out, Proc_q, Update_Mem, Zero_Time;
  wire [3:0] counter_1_q, multiplexer_1_out, subtractor_1_out;
  wire [31:0] register_1_q, register_2_q, register_3_q, register_4_q, register_5_q;

  // Probe on 4'b0011
  // Probe on 4'b0010
  Multiplexer #(.width(4), .enable("false")) multiplexer_1 (
    .in0(4'b0011), .in1(4'b0010), .out(multiplexer_1_out), .sel(nRead_Write));
  or or_1 (or_1_out, Idle, Update_Mem);
  or or_2 (or_2_out, ~Chip_Select, Reset);  // OR_Gate
  Subtractor #(.width(4)) subtractor_1 (.a(multiplexer_1_out), .b(4'b0010), .out(subtractor_1_out));  // open: bin, bout
  D_Flip_Flop u_Idle (.clk(CLK), .D(or_1_out), .Q(Idle_q), .preset(or_2_out));  // open: Qn, en, reset
  Demultiplexer #(.enable("false")) demultiplexer_1 (.out0(Idle), .out1(Load0), .in(Idle_q), .sel(Changed));
  // Probe on counter_1_q
  Counter #(.width(4), .max('hf)) counter_1 (
    .load(Load), .D(subtractor_1_out), .count(Count), .Q(counter_1_q), .clk(CLK), .clr(or_3_out));  // open: carry
  or or_3 (or_3_out, ~Chip_Select, Reset);  // OR_Gate
  Comparator #(.width(4), .mode("unsigned")) comparator_1 (
    .a(4'b0000), .b(counter_1_q), .eq(Zero_Time));  // open: gt, lt
  or or_4 (or_4_out, Count, Load0, Load1);
  Register #(.width(32)) register_1 (.D(Data_In_0), .en(Chip_Select), .Q(register_1_q), .clk(CLK), .clr(or_5_out));
  or or_5 (or_5_out, ~Chip_Select, Reset);  // OR_Gate
  Register #(.width(32)) register_2 (.D(Data_In_1), .en(Chip_Select), .Q(register_2_q), .clk(CLK), .clr(or_6_out));
  or or_6 (or_6_out, ~Chip_Select, Reset);  // OR_Gate
  Register #(.width(32)) register_3 (.D(Data_In_2), .en(Chip_Select), .Q(register_3_q), .clk(CLK), .clr(or_7_out));
  or or_7 (or_7_out, ~Chip_Select, Reset);  // OR_Gate
  Register #(.width(32)) register_4 (.D(Data_In_3), .en(Chip_Select), .Q(register_4_q), .clk(CLK), .clr(or_8_out));
  or or_8 (or_8_out, ~Chip_Select, Reset);  // OR_Gate
  Register #(.width(32)) register_5 (
    .D({{11{1'b1}}, nRead_Write, Mask, Address}), .en(Chip_Select), .Q(register_5_q), .clk(CLK),
    .clr(or_9_out));
  or or_9 (or_9_out, ~Chip_Select, Reset);  // OR_Gate
  D_Flip_Flop Proc (.clk(CLK), .D(or_4_out), .Q(Proc_q), .reset(or_10_out));  // open: Qn, preset, en
  or or_10 (or_10_out, ~Chip_Select, Reset);  // OR_Gate
  Demultiplexer #(.enable("false")) demultiplexer_2 (
    .out0(Count), .out1(Update_Mem), .in(demultiplexer_3_out0), .sel(Zero_Time));
  Demultiplexer #(.enable("false")) demultiplexer_3 (
    .out0(demultiplexer_3_out0), .out1(Load1), .in(Proc_q), .sel(Changed));
  Clock clock_1 (.out(CLK));
  Comparator #(.width(32)) comparator_2 (.a(register_1_q), .b(Data_In_0), .eq(comparator_2_eq));  // open: gt, lt
  Comparator #(.width(32)) comparator_3 (.a(register_2_q), .b(Data_In_1), .eq(comparator_3_eq));  // open: gt, lt
  Comparator #(.width(32)) comparator_4 (.a(register_3_q), .b(Data_In_2), .eq(comparator_4_eq));  // open: gt, lt
  Comparator #(.width(32)) comparator_5 (.a(register_4_q), .b(Data_In_3), .eq(comparator_5_eq));  // open: gt, lt
  Comparator #(.width(32)) comparator_6 (
    .a(register_5_q), .b({{11{1'b1}}, nRead_Write, Mask, Address}), .eq(comparator_6_eq));  // open: gt, lt
  nand nand_1 (nand_1_out, comparator_6_eq, comparator_2_eq, comparator_3_eq, comparator_4_eq, comparator_5_eq);
  and and_1 (Changed, nand_1_out, Chip_Select);
  or or_11 (Load, Count, Load1, Load0);
  and and_2 (and_2_out, Mask[0], Update_Mem, nRead_Write);
  and and_3 (and_3_out, Mask[1], Update_Mem, nRead_Write);
  and and_4 (and_4_out, Mask[2], Update_Mem, nRead_Write);
  and and_5 (and_5_out, Mask[3], Update_Mem, nRead_Write);
  RAM_part #(.addrWidth(16), .dataWidth(32), .bus("separate")) ram_1 (
    .addr(Address), .din(Data_In_0), .data(Data_Out_0), .str(and_2_out), .sel(Chip_Select), .clk(CLK),
    .ld(and_6_out), .clr(Reset));
  and and_6 (and_6_out, ~nRead_Write, Idle);  // AND_Gate
  RAM_part #(.addrWidth(16), .dataWidth(32), .bus("separate")) ram_2 (
    .addr(Address), .din(Data_In_1), .data(Data_Out_1), .str(and_3_out), .sel(Chip_Select), .clk(CLK),
    .ld(and_7_out), .clr(Reset));
  and and_7 (and_7_out, ~nRead_Write, Idle);  // AND_Gate
  RAM_part #(.addrWidth(16), .dataWidth(32), .bus("separate")) ram_3 (
    .addr(Address), .din(Data_In_2), .data(Data_Out_2), .str(and_4_out), .sel(Chip_Select), .clk(CLK),
    .ld(and_8_out), .clr(Reset));
  and and_8 (and_8_out, ~nRead_Write, Idle);  // AND_Gate
  RAM_part #(.addrWidth(16), .dataWidth(32), .bus("separate")) ram_4 (
    .addr(Address), .din(Data_In_3), .data(Data_Out_3), .str(and_5_out), .sel(Chip_Select), .clk(CLK),
    .ld(and_9_out), .clr(Reset));
  and and_9 (and_9_out, ~nRead_Write, Idle);  // AND_Gate

  assign Read_Time = 4'b0011;
  assign Write_Time = 4'b0010;

  // Other names for the same wires on the sheet: M0 = Mask[0]; M1 = Mask[1]; M2 = Mask[2]; M3 = Mask[3];
  //   RW = nRead_Write; CLR = Reset; CS = Chip_Select; Load2 = Count

  // Notes on the sheet:
  //   NO MODIFICAR
  //   excepto quizás los valores RT y WT
  //   BANK0
  //   BANK1
  //   BANK2
  //   BANK3
endmodule

module RAM_Dispatcher (
  input  [3:0] WriteTime,
  input  Clock,
  input  CLR,
  output [31:0] Data,
  output [15:0] Address,
  output [3:0] Mask,
  output Finished,
  output Write
);

  wire demultiplexer_2_out1, demultiplexer_3_out1, End, IDLE_q, IncAddr, Load, or_1_out, or_2_out, While_q,
       WriteEnd;
  wire [3:0] counter_1_q;
  wire [31:0] CurrentAddress_q;

  Counter #(.width(32), .max('hffffffff)) CurrentAddress (
    .count(IncAddr), .Q({CurrentAddress_q[31:18], Address, CurrentAddress_q[1:0]}), .clk(Clock), .clr(CLR));  // open: load, D, carry
  or or_1 (or_1_out, IncAddr, demultiplexer_3_out1, Finished);
  D_Flip_Flop IDLE (.clk(Clock), .D(or_1_out), .Q(IDLE_q), .preset(CLR));  // open: Qn, en, reset
  Demultiplexer #(.enable("false")) demultiplexer_1 (.out0(Load), .out1(Finished), .in(IDLE_q), .sel(End));
  D_Flip_Flop While (.clk(Clock), .D(or_2_out), .Q(While_q), .reset(CLR));  // open: Qn, preset, en
  or or_2 (or_2_out, Write, Load);
  RAM_part #(.addrWidth(18), .dataWidth(32)) ram_1 (
    .addr({Address, CurrentAddress_q[1:0]}), .data(Data), .clk(Clock));  // open: sel, ld, clr
  Demultiplexer #(.enable("false")) demultiplexer_2 (
    .out0(Write), .out1(demultiplexer_2_out1), .in(While_q), .sel(WriteEnd));
  Decoder_part #(.select(2)) decoder_1 (
    .out0(Mask[0]), .out1(Mask[1]), .out2(Mask[2]), .out3(Mask[3]), .sel(CurrentAddress_q[1:0]));  // open: en
  Demultiplexer #(.enable("false")) demultiplexer_3 (
    .out0(IncAddr), .out1(demultiplexer_3_out1), .in(demultiplexer_2_out1), .sel(End));
  Counter #(.width(4), .max('hf)) counter_1 (
    .load(Load), .D(WriteTime), .count(Write), .Q(counter_1_q), .clk(Clock));  // open: carry, clr
  Comparator #(.width(32)) comparator_1 (.a(Data), .b({32{1'b1}}), .eq(End));  // open: gt, lt
  Comparator #(.width(4)) comparator_2 (.a(4'b0000), .b(counter_1_q), .eq(WriteEnd));  // open: gt, lt

  // Other names for the same wires on the sheet: CLK = Clock; Count = Write; WT[3:0] = WriteTime
endmodule

module S_MIPS (
  input  Kbd_Available,
  input  [6:0] Kbd_ASCII_Data,
  input  [31:0] RAM_Out_0,
  input  [31:0] RAM_Out_1,
  input  Reset,
  input  [31:0] RAM_Out_2,
  input  Clock,
  input  [31:0] RAM_Out_3,
  input  [3:0] Read_Time,
  input  [3:0] Write_Time,
  output Kbd_Enable,
  output [15:0] Address,
  output Kbd_Clear,
  output TTY_Enable,
  output [6:0] TTY_ASCII_Data,
  output Stop,
  output [31:0] RAM_In_0,
  output [31:0] RAM_In_1,
  output [31:0] RAM_In_2,
  output [31:0] RAM_In_3,
  output [3:0] Mask,
  output nRead_Write,
  output Chip_Select
);

  wire fetcher_1_ready;
  wire [31:0] undriven;

  Fetcher fetcher_1 (
    .Clock(Clock), .Address(undriven), .Block_0(RAM_Out_0), .Block_1(RAM_Out_1), .Block_2(RAM_Out_2),
    .Block_3(RAM_Out_3), .RT(Read_Time), .Clear(Reset), .Ready(fetcher_1_ready), .Read(Chip_Select),
    .Address_2(Address));  // open: Word_out, Byte_Out
  // Decoder decoder_1: pin names not known; wires that end beside it: Clock, Stop

  assign Mask = 4'b0000;
  assign nRead_Write = 1'b0;

  // Other names for the same wires on the sheet: CLK = Clock; CLR = Reset; CS = Chip_Select;
  //   KBD_AVAIL = Kbd_Available; KBD_CLR = Kbd_Clear; KBD_DATA[6:0] = Kbd_ASCII_Data; RAM_A[15:0] = Address;
  //   RAM_OUTPUT_0[31:0] = RAM_Out_0; RAM_OUTPUT_1[31:0] = RAM_Out_1; RAM_OUTPUT_2[31:0] = RAM_Out_2;
  //   RAM_OUTPUT_3[31:0] = RAM_Out_3; TTY_DATA[6:0] = TTY_ASCII_Data

  // Notes on the sheet:
  //   RAM ADDRESS
  //   DATA FROM RAM
  //   DATA TO RAM
  //   DATA WRITE MASK
  //   RAM TIMING
  //   RAM CONTROL
  //   KEYBOARD
  //   TTY
  //   SEQUENCING
endmodule

module Fetcher_Last (
  input  Clock,
  input  Write,
  input  [15:0] Data,
  input  Fill,
  output [15:0] Output
);

  wire or_1_out, or_2_out;
  wire [15:0] multiplexer_1_out;

  or or_1 (or_1_out, Clock, Fill);
  or or_2 (or_2_out, Write, Fill);
  Multiplexer #(.width(16), .enable("false")) multiplexer_1 (
    .in0(Data), .in1({16{1'b1}}), .out(multiplexer_1_out), .sel(Fill));
  Register #(.width(16), .trigger("high")) register_1 (
    .D(multiplexer_1_out), .en(or_2_out), .Q(Output), .clk(or_1_out));  // open: clr
endmodule

module Fetcher_Load (
  input  Clock,
  input  [31:0] Block_0,
  input  [31:0] Block_1,
  input  [31:0] Block_2,
  input  [31:0] Block_3,
  input  Write,
  output [31:0] Block_0_2,
  output [31:0] Block_1_2,
  output [31:0] Block_2_2,
  output [31:0] Block_3_2
);

  Register #(.width(32)) register_1 (.D(Block_0), .en(Write), .Q(Block_0_2), .clk(Clock));  // open: clr
  Register #(.width(32)) register_2 (.D(Block_1), .en(Write), .Q(Block_1_2), .clk(Clock));  // open: clr
  Register #(.width(32)) register_3 (.D(Block_2), .en(Write), .Q(Block_2_2), .clk(Clock));  // open: clr
  Register #(.width(32)) register_4 (.D(Block_3), .en(Write), .Q(Block_3_2), .clk(Clock));  // open: clr
endmodule

module Fetcher (
  input  Clock,
  input  [31:0] Address,
  input  [31:0] Block_0,
  input  [31:0] Block_1,
  input  [31:0] Block_2,
  input  [31:0] Block_3,
  input  [3:0] RT,
  input  Clear,
  output Ready,
  output Read,
  output [15:0] Address_2,
  output [31:0] Word_out,
  output [7:0] Byte_Out
);

  wire comparator_2_eq, or_1_out;
  wire [3:0] counter_1_q;
  wire [15:0] fetcher_last_1_output;
  wire [31:0] fetcher_load_1_block_0_2, fetcher_load_1_block_1_2, fetcher_load_1_block_2_2,
       fetcher_load_1_block_3_2;

  Fetcher_Last fetcher_last_1 (
    .Clock(Clock), .Write(comparator_2_eq), .Data(Address[19:4]), .Fill(Clear), .Output(fetcher_last_1_output));
  Counter #(.width(4), .max('hf)) counter_1 (
    .Q(counter_1_q), .clk(Clock), .clr(or_1_out));  // open: load, D, count, carry
  or or_1 (or_1_out, Clear, Ready);
  Fetcher_Load fetcher_load_1 (
    .Clock(Clock), .Block_0(Block_0), .Block_1(Block_1), .Block_2(Block_2), .Block_3(Block_3), .Write(Read),
    .Block_0_2(fetcher_load_1_block_0_2), .Block_1_2(fetcher_load_1_block_1_2),
    .Block_2_2(fetcher_load_1_block_2_2), .Block_3_2(fetcher_load_1_block_3_2));
  not not_1 (Read, Ready);
  Comparator #(.width(16), .mode("unsigned")) comparator_1 (
    .a(fetcher_last_1_output), .b(Address[19:4]), .eq(Ready));  // open: gt, lt
  Comparator #(.width(4), .mode("unsigned")) comparator_2 (
    .a(counter_1_q), .b(RT), .eq(comparator_2_eq));  // open: gt, lt
  BitSelector #(.width(32), .group(8)) bitselector_1 (.in(Word_out), .out(Byte_Out), .sel(Address[1:0]));
  Multiplexer #(.select(2), .width(32), .enable("false")) multiplexer_1 (
    .in0(fetcher_load_1_block_0_2), .in1(fetcher_load_1_block_1_2), .in2(fetcher_load_1_block_2_2),
    .in3(fetcher_load_1_block_3_2), .out(Word_out), .sel(Address[3:2]));

  assign Address_2 = Address[19:4];
endmodule

module Decoder_Branch (
  input  Enable,
  input  d,
  input  e,
  input  f,
  output Invalid,
  output bltz,
  output beq,
  output bne,
  output blez,
  output bgtz
);

  wire decoder_1_out0, decoder_1_out2, decoder_1_out3;

  Decoder_part #(.select(3), .disabled(0)) decoder_1 (
    .out0(decoder_1_out0), .out1(bltz), .out2(decoder_1_out2), .out3(decoder_1_out3), .out4(beq), .out5(bne),
    .out6(blez), .out7(bgtz), .sel({d, e, f}), .en(Enable));
  or or_1 (Invalid, decoder_1_out0, decoder_1_out2, decoder_1_out3);
endmodule

module Decoder_Functions (
  input  Enable,
  input  a,
  input  b,
  input  c,
  input  d,
  input  e,
  input  f,
  output Invalid,
  output add,
  output sub,
  output \and ,
  output \or ,
  output \nor ,
  output \xor ,
  output mul,
  output mulu,
  output div,
  output divu,
  output slt,
  output sltu,
  output mfhi,
  output mflo,
  output jr
);

  wire and_1_out, decoder_1_out0, decoder_1_out1, decoder_1_out2, decoder_1_out3, decoder_1_out5,
       decoder_1_out6, decoder_1_out7, decoder_2_out3, decoder_2_out4, decoder_2_out6, decoder_3_out1,
       decoder_3_out3, decoder_3_out4, decoder_3_out5, decoder_3_out7, decoder_4_out1, decoder_4_out3,
       decoder_4_out4, decoder_4_out5, decoder_4_out6, decoder_4_out7, decoder_5_out1, decoder_5_out3,
       decoder_5_out5, decoder_5_out7, or_1_out, or_3_out, or_4_out, or_5_out, or_6_out, or_7_out, or_8_out;
  wire [2:0] buffer_1_out;

  Decoder_part #(.select(3), .disabled(0)) decoder_1 (
    .out0(decoder_1_out0), .out1(decoder_1_out1), .out2(decoder_1_out2), .out3(decoder_1_out3), .out4(jr),
    .out5(decoder_1_out5), .out6(decoder_1_out6), .out7(decoder_1_out7), .sel({c, b, a}), .en(Enable));
  or or_1 (or_1_out, jr, decoder_1_out0);
  or or_2 (Invalid, and_1_out, decoder_1_out3, decoder_1_out7, or_3_out);
  or or_3 (or_3_out, or_5_out, or_6_out, decoder_2_out3, decoder_2_out4, decoder_2_out6);
  assign buffer_1_out = {f, e, d};  // Buffer buffer_1, 3 bits wide
  and and_1 (and_1_out, or_1_out, or_4_out);
  or or_4 (or_4_out, buffer_1_out[2], buffer_1_out[1], buffer_1_out[0]);
  or or_5 (or_5_out, decoder_4_out1, decoder_4_out3, decoder_4_out4, decoder_4_out5, decoder_4_out6, decoder_4_out7, or_7_out);
  Decoder_part #(.select(3), .disabled(0)) decoder_2 (
    .out0(add), .out1(\and ), .out2(sub), .out3(decoder_2_out3), .out4(decoder_2_out4), .out5(\or ),
    .out6(decoder_2_out6), .out7(\nor ), .sel({f, e, d}), .en(decoder_1_out1));
  Decoder_part #(.select(3), .disabled(0)) decoder_3 (
    .out0(\xor ), .out1(decoder_3_out1), .out2(slt), .out3(decoder_3_out3), .out4(decoder_3_out4),
    .out5(decoder_3_out5), .out6(sltu), .out7(decoder_3_out7), .sel({f, e, d}), .en(decoder_1_out5));
  Decoder_part #(.select(3), .disabled(0)) decoder_4 (
    .out0(mfhi), .out1(decoder_4_out1), .out2(mflo), .out3(decoder_4_out3), .out4(decoder_4_out4),
    .out5(decoder_4_out5), .out6(decoder_4_out6), .out7(decoder_4_out7), .sel({f, e, d}), .en(decoder_1_out2));
  Decoder_part #(.select(3), .disabled(0)) decoder_5 (
    .out0(mul), .out1(decoder_5_out1), .out2(div), .out3(decoder_5_out3), .out4(mulu), .out5(decoder_5_out5),
    .out6(divu), .out7(decoder_5_out7), .sel(buffer_1_out), .en(decoder_1_out6));
  or or_6 (or_6_out, decoder_3_out4, decoder_3_out3, decoder_3_out1, decoder_3_out5, decoder_3_out7);
  or or_7 (or_7_out, or_8_out, decoder_5_out1);
  or or_8 (or_8_out, decoder_5_out7, decoder_5_out5, decoder_5_out3);
endmodule

module Decoder_Inmediate (
  input  Enable,
  input  a,
  input  b,
  input  c,
  input  d,
  input  e,
  input  f,
  output Invalid,
  output Branch,
  output lw,
  output sw,
  output addi,
  output andi,
  output ori,
  output xori,
  output slti,
  output sltui
);

  wire and_1_out, decoder_1_out1, decoder_1_out2, decoder_1_out3, decoder_1_out4, decoder_1_out5,
       decoder_1_out6, decoder_1_out7, decoder_2_out1, decoder_2_out7, nand_1_out, or_1_out, or_2_out;

  Decoder_part #(.select(3), .disabled(0)) decoder_1 (
    .out0(Branch), .out1(decoder_1_out1), .out2(decoder_1_out2), .out3(decoder_1_out3),
    .out4(decoder_1_out4), .out5(decoder_1_out5), .out6(decoder_1_out6), .out7(decoder_1_out7),
    .sel({c, b, a}), .en(Enable));
  Decoder_part #(.select(3), .disabled(0)) decoder_2 (
    .out0(addi), .out1(decoder_2_out1), .out2(slti), .out3(sltui), .out4(andi), .out5(ori), .out6(xori),
    .out7(decoder_2_out7), .sel({d, e, f}), .en(decoder_1_out4));
  or or_1 (or_1_out, decoder_1_out1, decoder_1_out5);
  nand nand_1 (nand_1_out, f, e, ~d);  // NAND_Gate
  and and_1 (and_1_out, or_1_out, nand_1_out);
  or or_2 (or_2_out, and_1_out, decoder_2_out1, decoder_2_out7);
  or or_3 (Invalid, decoder_1_out2, decoder_1_out3, decoder_1_out6, decoder_1_out7, or_2_out);
  and and_2 (lw, decoder_1_out1, ~and_1_out);  // AND_Gate
  and and_3 (sw, decoder_1_out5, ~and_1_out);  // AND_Gate
endmodule

module Decoder_Opcode (
  input  a,
  input  b,
  input  c,
  input  d,
  input  e,
  input  f,
  output Invalid,
  output Function,
  output Special,
  output Stack,
  output Jump,
  output Inmediate
);

  wire and_1_out, and_2_out, and_3_out, and_4_out, and_5_out, and_6_out, and_7_out, and_8_out, and_9_out,
       and_10_out, and_11_out, and_12_out, and_15_out, nand_1_out, nor_1_out, nor_2_out, not_1_out,
       not_2_out, not_3_out, not_4_out, not_5_out, not_6_out, not_7_out, not_8_out, not_9_out, or_1_out,
       or_2_out, or_3_out, or_5_out;

  not not_1 (not_1_out, d);
  nand nand_1 (nand_1_out, d, e);
  and and_1 (and_1_out, a, b, c);
  nor nor_1 (nor_1_out, a, b, c);
  not not_2 (not_2_out, d);
  and and_2 (and_2_out, d, e, f);
  nor nor_2 (nor_2_out, d, e, f);
  not not_3 (not_3_out, f);
  not not_4 (not_4_out, e);
  not not_5 (not_5_out, f);
  not not_6 (not_6_out, a);
  or or_1 (or_1_out, and_1_out, nor_1_out);
  or or_2 (or_2_out, and_2_out, nor_2_out);
  and and_3 (and_3_out, not_2_out, not_3_out, e);
  or or_3 (or_3_out, d, and_4_out);
  and and_4 (and_4_out, not_1_out, not_4_out, f);
  and and_5 (and_5_out, not_1_out, e, f);
  not not_7 (not_7_out, b);
  and and_6 (and_6_out, and_5_out, not_7_out, a);
  and and_7 (and_7_out, not_7_out, not_8_out, c);
  not not_8 (not_8_out, a);
  and and_8 (and_8_out, not_6_out, or_1_out);
  and and_9 (and_9_out, a, or_2_out, or_1_out);
  and and_10 (and_10_out, not_2_out, or_2_out);
  and and_11 (and_11_out, d, or_2_out);
  and and_12 (and_12_out, and_7_out, nand_1_out, not_5_out);
  and and_13 (Function, and_8_out, and_10_out);
  not not_9 (not_9_out, and_11_out);
  and and_14 (Jump, and_8_out, and_3_out);
  and and_15 (and_15_out, and_8_out, or_3_out);
  or or_4 (Inmediate, and_15_out, and_6_out, and_12_out);
  or or_5 (or_5_out, and_9_out, Function);
  and and_16 (Special, and_9_out, and_11_out);
  and and_17 (Stack, and_9_out, not_9_out);
  nor nor_3 (Invalid, or_5_out, Inmediate, Jump);
endmodule

module Decoder_Specials (
  input  Enable,
  input  a,
  input  b,
  input  c,
  input  d,
  input  e,
  input  f,
  output Invalid,
  output halt,
  output kbd,
  output rnd,
  output tty
);

  wire and_1_out, and_2_out, and_3_out, and_4_out, and_5_out, and_6_out, and_7_out, and_8_out, and_9_out,
       and_13_out, and_14_out, and_15_out, nor_1_out, nor_2_out, or_1_out, or_2_out, or_3_out, xnor_1_out;

  and and_1 (and_1_out, a, Enable);
  and and_2 (and_2_out, b, Enable);
  and and_3 (and_3_out, c, Enable);
  and and_4 (and_4_out, d, Enable);
  and and_5 (and_5_out, e, Enable);
  and and_6 (and_6_out, f, Enable);
  and and_7 (and_7_out, and_1_out, and_2_out, and_3_out);
  nor nor_1 (nor_1_out, and_1_out, and_2_out, and_3_out);
  and and_8 (and_8_out, and_4_out, and_5_out, and_6_out);
  nor nor_2 (nor_2_out, and_4_out, and_5_out, and_6_out);
  NotExactlyOne xnor_1 (.out(xnor_1_out), .in0(and_4_out), .in1(and_5_out), .in2(and_6_out));
  or or_1 (or_1_out, xnor_1_out, nor_2_out, ~nor_1_out, and_8_out, and_7_out);  // OR_Gate
  and and_9 (and_9_out, nor_1_out, or_1_out);
  and and_10 (kbd, ~or_1_out, and_4_out);  // AND_Gate
  and and_11 (rnd, ~or_1_out, and_5_out);  // AND_Gate
  and and_12 (tty, ~or_1_out, and_6_out);  // AND_Gate
  or or_2 (or_2_out, and_9_out, or_3_out);
  or or_3 (or_3_out, and_13_out, and_14_out, and_15_out);
  and and_13 (and_13_out, and_7_out, ~and_8_out);  // AND_Gate
  and and_14 (and_14_out, and_7_out, ~and_8_out);  // AND_Gate
  and and_15 (and_15_out, or_1_out, ~and_7_out);  // AND_Gate
  and and_16 (Invalid, Enable, or_2_out);
  and and_17 (halt, ~or_2_out, and_7_out);  // AND_Gate
endmodule

module Decoder_Stack (
  input  Enable,
  input  d,
  input  e,
  input  f,
  output Invalid,
  output pop,
  output push
);

  wire and_1_out, or_1_out;

  or or_1 (or_1_out, d, e);
  and and_1 (and_1_out, ~or_1_out, Enable);  // AND_Gate
  Decoder_part #(.disabled(0)) decoder_1 (.out0(pop), .out1(push), .sel(f), .en(and_1_out));
  and and_2 (Invalid, Enable, or_1_out);
endmodule

module Decoder (
  input  Clock,
  input  [31:0] Instruction,
  input  Ready,
  input  [31:0] R1,
  input  [31:0] R2,
  input  [31:0] R3,
  input  Reset,
  input  [31:0] Result,
  input  Condition,
  output Invalid,
  output halt,
  output [4:0] S_R1,
  output [4:0] S_R2,
  output [4:0] S_R3,
  output [31:0] OP1,
  output [31:0] OP2,
  output [31:0] OP3,
  output [3:0] ALU_code,
  output Activate_ALU,
  output [31:0] PC
);

  wire adder_1_cout, and_1_out, decoder_branch_1_beq, decoder_branch_1_bgtz, decoder_branch_1_blez,
       decoder_branch_1_bltz, decoder_branch_1_bne, decoder_branch_1_invalid, decoder_functions_1_add,
       decoder_functions_1_and, decoder_functions_1_div, decoder_functions_1_divu,
       decoder_functions_1_invalid, decoder_functions_1_jr, decoder_functions_1_mul,
       decoder_functions_1_mulu, decoder_functions_1_nor, decoder_functions_1_or, decoder_functions_1_slt,
       decoder_functions_1_sltu, decoder_functions_1_sub, decoder_functions_1_xor, decoder_inmediate_1_addi,
       decoder_inmediate_1_andi, decoder_inmediate_1_branch, decoder_inmediate_1_invalid,
       decoder_inmediate_1_ori, decoder_inmediate_1_slti, decoder_inmediate_1_sltui,
       decoder_inmediate_1_xori, decoder_opcode_1_function, decoder_opcode_1_inmediate,
       decoder_opcode_1_invalid, decoder_opcode_1_special, decoder_opcode_1_stack,
       decoder_specials_1_invalid, decoder_stack_1_invalid, or_3_out, or_4_out, or_5_out, or_6_out, or_7_out,
       or_8_out, or_9_out;
  wire [1:0] decoder_opcode_1_jump;
  wire [7:2] multiplexer_1_out;
  wire [10:0] multiplexer_1_out_2;
  wire [31:0] adder_1_out, multiplexer_2_out, multiplexer_3_out;

  Multiplexer #(.width(32), .enable("false")) multiplexer_1 (
    .in0({32{1'b0}}), .in1(Instruction),
    .out({multiplexer_1_out_2[7:0], S_R3, multiplexer_1_out_2[10:8], S_R1[2:0], S_R2, multiplexer_1_out, S_R1[4:3]}),
    .sel(Ready));
  and and_1 (and_1_out, Ready, Clock);
  or or_1 (Invalid, adder_1_cout, decoder_stack_1_invalid, decoder_specials_1_invalid, decoder_functions_1_invalid, decoder_branch_1_invalid, decoder_inmediate_1_invalid, decoder_opcode_1_invalid);
  Multiplexer #(.select(2), .width(32), .enable("false")) multiplexer_2 (
    .in0(adder_1_out), .in1({{6{1'b0}}, S_R1, S_R2, S_R3, multiplexer_1_out_2}), .in2(multiplexer_3_out),
    .in3({32{1'b0}}), .out(multiplexer_2_out), .sel(decoder_opcode_1_jump));
  Register #(.width(32)) register_1 (.D(multiplexer_2_out), .Q(PC), .clk(and_1_out), .clr(Reset));  // open: en
  Decoder_Opcode decoder_opcode_1 (
    .a(multiplexer_1_out[7]), .b(multiplexer_1_out[6]), .c(multiplexer_1_out[5]), .d(multiplexer_1_out[4]),
    .e(multiplexer_1_out[3]), .f(multiplexer_1_out[2]), .Invalid(decoder_opcode_1_invalid),
    .Function(decoder_opcode_1_function), .Special(decoder_opcode_1_special), .Stack(decoder_opcode_1_stack),
    .Jump(decoder_opcode_1_jump[0]), .Inmediate(decoder_opcode_1_inmediate));
  Adder #(.width(32)) adder_1 (.a(PC), .b(32'h4), .out(adder_1_out), .cout(adder_1_cout));  // open: cin
  Decoder_Inmediate decoder_inmediate_1 (
    .Enable(decoder_opcode_1_inmediate), .a(multiplexer_1_out[7]), .b(multiplexer_1_out[6]),
    .c(multiplexer_1_out[5]), .d(multiplexer_1_out[4]), .e(multiplexer_1_out[3]), .f(multiplexer_1_out[2]),
    .Invalid(decoder_inmediate_1_invalid), .Branch(decoder_inmediate_1_branch),
    .addi(decoder_inmediate_1_addi), .andi(decoder_inmediate_1_andi), .ori(decoder_inmediate_1_ori),
    .xori(decoder_inmediate_1_xori), .slti(decoder_inmediate_1_slti), .sltui(decoder_inmediate_1_sltui));  // open: lw, sw
  Multiplexer #(.width(32), .disabled(0), .enable("false")) multiplexer_3 (
    .in0({{14{1'b0}}, S_R3, multiplexer_1_out_2, 2'b00}), .out(multiplexer_3_out),
    .sel(decoder_functions_1_jr));  // open: in1
  // OR_Gate or_2 has open pins: in0=decoder_functions_1_jr, in1=Condition, out=open
  Decoder_Branch decoder_branch_1 (
    .d(multiplexer_1_out[4]), .e(multiplexer_1_out[3]), .f(multiplexer_1_out[2]),
    .Invalid(decoder_branch_1_invalid), .bltz(decoder_branch_1_bltz), .beq(decoder_branch_1_beq),
    .bne(decoder_branch_1_bne), .blez(decoder_branch_1_blez), .bgtz(decoder_branch_1_bgtz),
    .Enable(decoder_inmediate_1_branch));
  or or_3 (or_3_out, decoder_branch_1_beq, decoder_branch_1_bne);
  Decoder_Functions decoder_functions_1 (
    .Enable(decoder_opcode_1_function), .a(multiplexer_1_out_2[5]), .b(multiplexer_1_out_2[4]),
    .c(multiplexer_1_out_2[3]), .d(multiplexer_1_out_2[2]), .e(multiplexer_1_out_2[1]),
    .f(multiplexer_1_out_2[0]), .Invalid(decoder_functions_1_invalid), .add(decoder_functions_1_add),
    .sub(decoder_functions_1_sub), .\and (decoder_functions_1_and), .\or (decoder_functions_1_or),
    .\nor (decoder_functions_1_nor), .\xor (decoder_functions_1_xor), .mul(decoder_functions_1_mul),
    .mulu(decoder_functions_1_mulu), .div(decoder_functions_1_div), .divu(decoder_functions_1_divu),
    .slt(decoder_functions_1_slt), .sltu(decoder_functions_1_sltu), .jr(decoder_functions_1_jr));  // open: mfhi, mflo
  Decoder_Specials decoder_specials_1 (
    .Enable(decoder_opcode_1_special), .a(multiplexer_1_out[7]), .b(multiplexer_1_out[6]),
    .c(multiplexer_1_out[5]), .d(multiplexer_1_out[4]), .e(multiplexer_1_out[3]), .f(multiplexer_1_out[2]),
    .Invalid(decoder_specials_1_invalid), .halt(halt));  // open: kbd, rnd, tty
  Decoder_Stack decoder_stack_1 (
    .Enable(decoder_opcode_1_stack), .d(multiplexer_1_out[5]), .e(multiplexer_1_out[6]),
    .f(multiplexer_1_out[7]), .Invalid(decoder_stack_1_invalid));  // open: pop, push
  or or_4 (or_4_out, decoder_inmediate_1_addi, decoder_functions_1_add);
  or or_5 (or_5_out, decoder_inmediate_1_andi, decoder_functions_1_and);
  or or_6 (or_6_out, decoder_inmediate_1_ori, decoder_functions_1_or);
  or or_7 (or_7_out, decoder_inmediate_1_xori, decoder_functions_1_xor);
  or or_8 (or_8_out, decoder_inmediate_1_slti, decoder_functions_1_slt);
  or or_9 (or_9_out, decoder_inmediate_1_sltui, decoder_functions_1_sltu);
  // Priority_Encoder #(.select(4), .disabled(0)) priority_encoder_1: pin names not known; wires that end beside it: or_4_out, decoder_functions_1_sub, or_5_out, or_6_out, decoder_functions_1_nor, or_7_out, decoder_functions_1_mul, decoder_functions_1_mulu, ALU_code, decoder_functions_1_div, Activate_ALU, decoder_functions_1_divu, or_8_out, or_9_out, or_3_out, decoder_branch_1_blez, decoder_branch_1_bgtz, decoder_branch_1_bltz, OP1, OP2
endmodule
